// Logisim project processor2.circ as structural Verilog
module ALU (
  input  [2:0] F,
  input  [31:0] B,
  input  [31:0] A,
  output Zero,
  output [31:0] Y
);

  wire bitselector_1_out;
  wire [31:0] adder_1_out, and_1_out, bit_extender_1_out, multiplexer_1_out, multiplier_1_out, negator_1_out,
       or_1_out;

  Multiplier #(.width(32)) multiplier_1 (.a(B), .b(A), .out(multiplier_1_out));  // open: cin, cout
  Negator #(.width(32)) negator_1 (.in(B), .out(negator_1_out));
  assign or_1_out = B | A;  // OR_Gate or_1, 32 bits wide
  Adder #(.width(32)) adder_1 (.a(A), .b(multiplexer_1_out), .out(adder_1_out));  // open: cin, cout
  Multiplexer #(.width(32), .enable("false")) multiplexer_1 (
    .in0(B), .in1(negator_1_out), .out(multiplexer_1_out), .sel(F[2]));
  BitSelector #(.width(32)) bitselector_1 (.in(adder_1_out), .out(bitselector_1_out), .sel({5{1'b1}}));
  assign and_1_out = B & A;  // AND_Gate and_1, 32 bits wide
  assign bit_extender_1_out = {{31{1'b0}}, bitselector_1_out};  // Bit_Extender bit_extender_1
  Multiplexer #(.select(3), .width(32), .enable("false")) multiplexer_2 (
    .in0(and_1_out), .in1(or_1_out), .in2(adder_1_out), .in3(multiplier_1_out), .in6(adder_1_out),
    .in7(bit_extender_1_out), .out(Y), .sel(F));  // open: in4, in5
  Comparator #(.width(32), .mode("unsigned")) comparator_1 (.a({32{1'b0}}), .b(Y), .eq(Zero));  // open: gt, lt
endmodule

module Datapath (
  output [31:0] out_1,
  output [31:0] v0
);

  wire alu_1_zero, Branch_AND_out, clock_1_out, controlunit_1_alusrc, controlunit_1_branch,
       controlunit_1_regdst, controlunit_1_regwrite;
  wire [2:0] bitselector_1_out, bitselector_2_out, bitselector_5_out, bitselector_7_out,
       controlunit_1_alucontrol, multiplexer_2_out;
  wire [7:0] adder_1_out, adder_2_out, bitselector_4_out, bitselector_9_out, multiplexer_1_out, register_1_q,
       shifter_1_out;
  wire [15:0] bitselector_3_out, bitselector_6_out, bitselector_8_out;
  wire [31:0] alu_1_y, bit_extender_1_out, multiplexer_3_out, registerfile_1_rd1, registerfile_1_rd2,
       shifter_2_out;

  Clock clock_1 (.out(clock_1_out));
  Multiplexer #(.width(8), .enable("false")) multiplexer_1 (
    .in0(adder_1_out), .in1(adder_2_out), .out(multiplexer_1_out), .sel(Branch_AND_out));
  Register register_1 (.D(multiplexer_1_out), .Q(register_1_q), .clk(clock_1_out));  // open: en, clr
  Adder adder_1 (.a(register_1_q), .b(8'h4), .out(adder_1_out));  // open: cin, cout
  Shifter #(.shift("lr")) shifter_1 (.in(register_1_q), .\dist (3'b010), .out(shifter_1_out));
  ROM #(.dataWidth(32)) rom_1 (.addr(shifter_1_out), .data(out_1));  // open: sel
  BitSelector #(.width(32), .group(3)) bitselector_1 (.in(out_1), .out(bitselector_1_out), .sel(4'b0111));
  BitSelector #(.width(16), .group(3)) bitselector_2 (.in(bitselector_3_out), .out(bitselector_2_out), .sel(3'b000));
  BitSelector #(.width(32), .group(16)) bitselector_3 (.in(out_1), .out(bitselector_3_out), .sel(1'b1));
  BitSelector #(.width(32), .group(8)) bitselector_4 (.in(out_1), .out(bitselector_4_out), .sel(2'b01));
  and Branch_AND (Branch_AND_out, alu_1_zero, controlunit_1_branch);
  BitSelector #(.group(3)) bitselector_5 (.in(bitselector_4_out), .out(bitselector_5_out), .sel(2'b01));
  ControlUnit controlunit_1 (
    .Instruction(out_1), .RegDst(controlunit_1_regdst), .RegWrite(controlunit_1_regwrite),
    .ALUControl(controlunit_1_alucontrol), .Branch(controlunit_1_branch), .ALUSrc(controlunit_1_alusrc));
  RegisterFile registerfile_1 (
    .CLK(clock_1_out), .A1(bitselector_1_out), .WD3(alu_1_y), .A2(bitselector_2_out),
    .WE3(controlunit_1_regwrite), .RD1(registerfile_1_rd1), .RD2(registerfile_1_rd2), .A3(multiplexer_2_out),
    .V0(v0));
  BitSelector #(.width(32), .group(16)) bitselector_6 (.in(out_1), .out(bitselector_6_out), .sel(1'b1));
  BitSelector #(.width(16), .group(3)) bitselector_7 (.in(bitselector_6_out), .out(bitselector_7_out), .sel(3'b000));
  Multiplexer #(.width(3), .enable("false")) multiplexer_2 (
    .in0(bitselector_7_out), .in1(bitselector_5_out), .out(multiplexer_2_out), .sel(controlunit_1_regdst));
  assign bit_extender_1_out = {{16{bitselector_8_out[15]}}, bitselector_8_out};  // Bit_Extender bit_extender_1
  BitSelector #(.width(32), .group(16)) bitselector_8 (.in(out_1), .out(bitselector_8_out), .sel(1'b0));
  Multiplexer #(.width(32), .enable("false")) multiplexer_3 (
    .in0(registerfile_1_rd2), .in1(bit_extender_1_out), .out(multiplexer_3_out), .sel(controlunit_1_alusrc));
  Shifter #(.width(32)) shifter_2 (.in(bit_extender_1_out), .\dist (5'b00010), .out(shifter_2_out));
  BitSelector #(.width(32), .group(8)) bitselector_9 (.in(shifter_2_out), .out(bitselector_9_out), .sel(2'b00));
  ALU alu_1 (
    .F(controlunit_1_alucontrol), .B(multiplexer_3_out), .A(registerfile_1_rd1), .Y(alu_1_y),
    .Zero(alu_1_zero));
  Adder adder_2 (.a(bitselector_9_out), .b(adder_1_out), .out(adder_2_out));  // open: cin, cout

  // Notes on the sheet:
  //   contents of rom_1 (hex, n*v repeats v):
  //   20040008 20020001 1080000a 20010001 10240008 41020 2086ffff 10000001 20c6ffff 20010001 10260002
  //   70461002 1000fffb 1000ffff
  //   sign extend imm
  //   R2 or imm
endmodule

module Tests (
  output [31:0] Y,
  output [7:0] out_2,
  output [7:0] out_3,
  output [2:0] out_4
);

  BitSelector #(.width(32), .group(8)) bitselector_1 (.in(32'h12356789), .out(out_2), .sel(2'b00));
  BitSelector #(.width(32), .group(8)) bitselector_2 (.in(32'h12356789), .out(out_3), .sel(2'b01));
  BitSelector #(.group(3)) bitselector_3 (.in(out_3), .out(out_4), .sel(2'b00));

  assign Y = 32'hf4010207;

  // Notes on the sheet:
  //   binary values in Logisim. Convince yourself how the bits are displayed.
  //   Example 2: The bit selector is configured to have 32  
  //   bit group #1 (starting at index 0) is selected for the output.
  //   That is, the 8 bits 0x67 at bit indices 15..8  are sent to the output.
  //   Example 3: Now, assume that you want to extract 3 bits at   
  //   Example 1: A simple example that illustrates how 32-bit values are displayed as 
  //   input bits and 8 output bits. The parameter constant is 1, which means that   
  //   bit indices 10..8. This can be accoplished by putting two bit selecotrs in series.
endmodule

module RegisterFile (
  input  CLK,
  input  [2:0] A1,
  input  [31:0] WD3,
  input  [2:0] A2,
  input  WE3,
  input  [2:0] A3,
  output [31:0] RD1,
  output [31:0] RD2,
  output [31:0] V0
);

  wire and_1_out, and_2_out, and_3_out, and_4_out, and_5_out, and_6_out, and_7_out, decoder_1_out1,
       decoder_1_out2, decoder_1_out3, decoder_1_out4, decoder_1_out5, decoder_1_out6, decoder_1_out7;
  wire [31:0] a0_q, a1_q, a2_q, a3_q, at_q, v1_q;

  Decoder #(.select(3)) decoder_1 (
    .out1(decoder_1_out1), .out2(decoder_1_out2), .out3(decoder_1_out3), .out4(decoder_1_out4),
    .out5(decoder_1_out5), .out6(decoder_1_out6), .out7(decoder_1_out7), .sel(A3));  // open: out0, en
  and and_1 (and_1_out, WE3, decoder_1_out1);
  and and_2 (and_2_out, WE3, decoder_1_out2);
  and and_3 (and_3_out, WE3, decoder_1_out3);
  and and_4 (and_4_out, WE3, decoder_1_out4);
  and and_5 (and_5_out, WE3, decoder_1_out5);
  and and_6 (and_6_out, WE3, decoder_1_out6);
  and and_7 (and_7_out, WE3, decoder_1_out7);
  Register #(.width(32)) at (.D(WD3), .en(and_1_out), .Q(at_q), .clk(CLK));  // open: clr
  Register #(.width(32)) u_v0 (.D(WD3), .en(and_2_out), .Q(V0), .clk(CLK));  // open: clr
  Register #(.width(32)) v1 (.D(WD3), .en(and_3_out), .Q(v1_q), .clk(CLK));  // open: clr
  Register #(.width(32)) a0 (.D(WD3), .en(and_4_out), .Q(a0_q), .clk(CLK));  // open: clr
  Register #(.width(32)) u_a1 (.D(WD3), .en(and_5_out), .Q(a1_q), .clk(CLK));  // open: clr
  Register #(.width(32)) u_a2 (.D(WD3), .en(and_6_out), .Q(a2_q), .clk(CLK));  // open: clr
  Register #(.width(32)) u_a3 (.D(WD3), .en(and_7_out), .Q(a3_q), .clk(CLK));  // open: clr
  Multiplexer #(.select(3), .width(32)) multiplexer_1 (
    .in0({32{1'b0}}), .in1(at_q), .in2(V0), .in3(v1_q), .in4(a0_q), .in5(a1_q), .in6(a2_q), .in7(a3_q),
    .out(RD1), .sel(A1));  // open: en
  Multiplexer #(.select(3), .width(32)) multiplexer_2 (
    .in0({32{1'b0}}), .in1(at_q), .in2(V0), .in3(v1_q), .in4(a0_q), .in5(a1_q), .in6(a2_q), .in7(a3_q),
    .out(RD2), .sel(A2));  // open: en
endmodule

module ControlUnit (
  input  [31:0] Instruction,
  output RegDst,
  output RegWrite,
  output ALUSrc,
  output Branch,
  output [2:0] ALUControl
);

  wire comparator_2_eq, comparator_4_eq;
  wire [2:0] multiplexer_1_out;
  wire [5:0] bitselector_1_out;
  wire [31:0] shifter_1_out;

  Shifter #(.width(32), .shift("lr")) shifter_1 (.in(Instruction), .\dist (5'b11010), .out(shifter_1_out));
  BitSelector #(.width(32), .group(6)) bitselector_1 (.in(shifter_1_out), .out(bitselector_1_out), .sel(3'b000));
  Comparator #(.width(6), .mode("unsigned")) comparator_1 (
    .a(bitselector_1_out), .b(6'b001000), .eq(ALUSrc));  // open: gt, lt
  Comparator #(.width(6), .mode("unsigned")) comparator_2 (
    .a(bitselector_1_out), .b({6{1'b0}}), .eq(comparator_2_eq));  // open: gt, lt
  Comparator #(.width(6), .mode("unsigned")) comparator_3 (
    .a(bitselector_1_out), .b(6'b000100), .eq(Branch));  // open: gt, lt
  Comparator #(.width(6), .mode("unsigned")) comparator_4 (
    .a(bitselector_1_out), .b(6'b011100), .eq(comparator_4_eq));  // open: gt, lt
  or or_1 (RegDst, comparator_2_eq, comparator_4_eq);
  Multiplexer #(.width(3), .enable("false")) multiplexer_1 (
    .in0(3'b010), .in1(3'b011), .out(multiplexer_1_out), .sel(comparator_4_eq));
  or or_2 (RegWrite, ALUSrc, RegDst);
  Multiplexer #(.width(3), .enable("false")) multiplexer_2 (
    .in0(multiplexer_1_out), .in1(3'b110), .out(ALUControl), .sel(Branch));
endmodule
